// Digital circuit hw1_2-bit_multiplier.dig as structural Verilog
module hw1_2_bit_multiplier (
  input  [1:0] A,
  input  [1:0] B,
  output [3:0] P
);

  wire and_1_out, and_2_out, and_3_out, and_4_out, and_5_out, and_6_out;

  and and_1 (and_1_out, A[1], B[1], ~B[0]);  // And
  and and_2 (and_2_out, A[1], ~A[0], B[1]);  // And
  and and_3 (and_3_out, A[1], ~B[1], B[0]);  // And
  and and_4 (and_4_out, A[1], ~A[0], B[0]);  // And
  and and_5 (and_5_out, ~A[1], A[0], B[1]);  // And
  and and_6 (and_6_out, A[0], B[1], ~B[0]);  // And
  and and_7 (P[3], A[1], A[0], B[1], B[0]);
  or or_1 (P[2], and_1_out, and_2_out);
  or or_2 (P[1], and_3_out, and_4_out, and_5_out, and_6_out);
  and and_8 (P[0], A[0], B[0]);
endmodule
